# Fritzing sketch Skripsi (saved by Fritzing 0.9.3b)
circuit board: 11.6559cm x 6.60416cm

parts:
  J1 = Basic Servo  # not connected
  J2 = Basic Servo  # not connected
  J3 = Basic Servo  # not connected
  J4 = Basic Servo  # not connected
  J5 = Basic Servo  # not connected
  Part1 = 16-Channel 12-bit PCA9685 PWM/Servo Driver
  A1 = WeMos D1 R1

nets:
  N1: Part1.GND, A1.Pin_11, A1.Pin_14, A1.Pin_66
  N2: Part1.VCC, A1.Pin_7
  N3: Part1.SDA, A1.Pin_25, A1.Pin_70
  N4: Part1.SCL, A1.Pin_27, A1.Pin_72

custom parts:
  16-Channel 12-bit PCA9685 PWM/Servo Driver: The Adafruit 16-Channel 12-bit PWM/Servo Driver will drive up to 16 servos over I2C with only 2 pins. The on-board PCA9685 PWM controller will drive all 16 channels simultaneously with no additional processing overhead. What's more, you can chain up to 62 of them to control up to 992 servos - all with the same 2 pins
  WeMos D1 R1: The WeMos D1 is a ESP8266 WiFi based board that uses the Arduino layout with a operating voltage of 3.3V.
